# Fritzing sketch TLCv1 (saved by Fritzing 0.9.3b)
circuit board: 5.74153cm x 5.33254cm
breadboards: 1

parts:
  Status = RGB LED (com. cathode, rbg) [package="5 mm [THT]"]
  Pulse_Sensor = Header 3 [package=molex-1x3_lock]
  Effect_Toggle = Header 2 [package=molex-1x2_lock]
  Pwr_Swtch = Header 2 [package=molex-1x2_lock]
  Power_5-12v = Header 2 [package=molex-1x2_lock]
  Config = DIP Switch 4 Position [package=dipswitch-04]
  3_3v_o_5v = female pin header, 3 pins [form="♀ (female)"]
  G = Resistor [tolerance=±5% resistance=220 package="0603 [SMD]"]
  R = Resistor [tolerance=±5% resistance=220 package="0603 [SMD]"]
  B = Resistor [tolerance=±5% resistance=220 package="0603 [SMD]"]
  R24 = shrouded pin header, 8 pins [form="♂ (shrouded male)"]
  Nano = Arduino Nano (Rev3.0)
  J1 = female pin header, 15 pins [form="♀ (female)"]

nets:
  N1: Status.red_anode, R.Pin_1
  N2: Status.common_cathode, Pulse_Sensor.1, Effect_Toggle.2, Power_5-12v.2, Config.5, Config.6, Config.7, Config.8, R24.pin8, Nano.GND
  N3: Status.blue_anode, G.Pin_1
  N4: Status.green_anode, B.Pin_1
  N5: Pulse_Sensor.2, 3_3v_o_5v.pin3, Nano.5V
  N6: Pulse_Sensor.3, Nano.A7, J1.pin2
  N7: Effect_Toggle.1, Nano.D6
  N8: Pwr_Swtch.1, Nano.VIN
  N9: Pwr_Swtch.2, Power_5-12v.1
  N10: Config.1, Nano.D2, J1.pin15
  N11: Config.2, Nano.D3, J1.pin14
  N12: Config.3, Nano.D4, J1.pin13
  N13: Config.4, Nano.D5, J1.pin12
  N14: 3_3v_o_5v.pin1, Nano.3V3
  N15: 3_3v_o_5v.pin2, R24.pin1
  N16: G.Pin_0, Nano.A1, J1.pin8
  N17: R.Pin_0, Nano.A0, J1.pin9
  N18: B.Pin_0, Nano.A2, J1.pin7
  N19: R24.pin2, Nano.D9
  N20: R24.pin3, Nano.D11/MOSI
  N21: R24.pin5, Nano.D12/MISO
  N22: R24.pin6, Nano.D13/SCK
  N23: R24.pin7, Nano.D10
  N24: Nano.D7, J1.pin11
  N25: Nano.D8, J1.pin10
  N26: Nano.A6, J1.pin3
  N27: Nano.A5, J1.pin4
  N28: Nano.A4, J1.pin5
  N29: Nano.A3, J1.pin6
